# Fritzing sketch BirdTrapMechanism (saved by Fritzing 0.9.3b)
breadboards: 1

parts:
  Solenoid = Solenoid
  IR_Transmitter = Grove Infrared Emitter
  Coin_Battery_3V = FKIT-COIN_CELL [package=fkit-lir2450-h]
  Relay = Relay [part_number=FRS1B-S package=THT]
  R1 = Resistor [tolerance=±5% resistance=220 package=THT]
  R2 = Resistor [tolerance=±5% resistance=220 package=THT]
  IR_Receiver = Grove Infrared Receiver
  Battery = Battery block 9V
  Pushbutton = SWITCH-MOMENTARY-2 [package=tactile_switch_tall]

nets (from the schematic view):
  N1: Solenoid.pin1, Relay.COIL2, IR_Receiver.GND, Battery.-
  N2: Solenoid.pin2, R1.Pin_0
  N3: IR_Transmitter.GND, Coin_Battery_3V.NEG
  N4: IR_Transmitter.VCC, Pushbutton.2
  N5: Coin_Battery_3V.POS, Pushbutton.1
  N6: Relay.A, Relay.B, IR_Receiver.VCC, Battery.+
  N7: Relay.COIL1, IR_Receiver.RX
  N8: Relay.C1, Relay.C2, R2.Pin_0
  N9: R1.Pin_1, R2.Pin_1

custom parts:
  Relay: An SPDT relay.
